# Fritzing sketch CPLDintroduction (saved by Fritzing 0.9.3b)
breadboards: 1

parts:
  Part1 = Arduino Uno (Rev3) - ICSP
  C2 = Capacitor Polarized [package=cpol-radial-10uf-25v]
  C3 = Ceramic Capacitor [capacitance="100 nF" package="0603 [SMD, multilayer]"]
  LED1 = LED - 3mm [color="Red (633nm)" package="3 mm [THT]"]
  R1 = Resistor [tolerance=±5% resistance=330 package=THT]

nets:
  N1: Part1.5V, C2.+, C3.1
  N2: Part1.GND, C2.-, C3.0
  N3: LED1.anode, R1.Pin_1
